// Logisim project MileStone1_Team123.circ as structural Verilog: 1 circuit, main circuit main
module main (
  input  in_1,
  input  in_2,
  input  in_3
);

  wire adder_1_cout, and_2_out, and_3_out, and_4_out, and_5_out, and_6_out, and_7_out, and_8_out, and_9_out,
       and_10_out, and_11_out, and_12_out, and_13_out, and_14_out, and_15_out, and_16_out, and_17_out,
       bitselector_1_out, bitselector_5_out, Clock_out, comparator_1_eq, d_ff_2_q, decoder_1_out0,
       decoder_1_out1, decoder_1_out2, decoder_1_out3, decoder_1_out4, decoder_1_out5, decoder_1_out6,
       decoder_1_out7, decoder_2_out0, decoder_2_out1, decoder_2_out2, decoder_2_out3, decoder_2_out4,
       decoder_2_out5, decoder_2_out6, decoder_2_out7, decoder_2_out8, decoder_2_out9, decoder_2_out10,
       decoder_2_out11, decoder_2_out12, decoder_2_out13, decoder_2_out14, decoder_2_out15, I_FlipFlop_q,
       not_2_out, or_2_out, or_3_out, or_4_out, or_5_out, or_6_out, or_7_out, or_8_out, or_9_out, or_10_out,
       or_11_out, or_12_out, or_13_out, or_14_out;
  wire [2:0] bitselector_3_out, priority_encoder_1_out, priority_encoder_2_out;
  wire [3:0] bitselector_2_out, Sequence_Counter_q;
  wire [11:0] AR_q, bit_extender_1_out, bit_extender_3_out, bitselector_4_out, PC_q;
  wire [15:0] AC_q, adder_1_out, and_1_out, bit_extender_2_out, bit_extender_4_out, DR_q, IR_q,
       multiplexer_1_out, multiplexer_2_out, not_1_out, or_1_out, ram_1_data, subtractor_1_out, TR_q,
       xor_1_out;

  Subtractor #(.width(16)) subtractor_1 (.a(AC_q), .b(DR_q), .out(subtractor_1_out), .bin(in_2));  // open: bout
  Adder #(.width(16)) adder_1 (.a(AC_q), .b(DR_q), .out(adder_1_out), .cin(in_3), .cout(adder_1_cout));
  assign and_1_out = AC_q & DR_q;  // AND_Gate and_1, 16 bits wide
  D_Flip_Flop d_ff_1 (.clk(Clock_out), .D(adder_1_cout), .en(and_2_out));  // open: Q, Qn, preset, reset
  and and_2 (and_2_out, decoder_1_out1, decoder_2_out5);
  RAM #(.addrWidth(12), .dataWidth(16), .bus("separate")) ram_1 (
    .addr(AR_q), .din(multiplexer_2_out), .data(ram_1_data), .str(and_9_out), .clk(Clock_out), .ld(or_6_out));  // open: sel, clr
  assign or_1_out = AC_q | DR_q;  // OR_Gate or_1, 16 bits wide
  Register #(.width(16)) IR (.D(multiplexer_2_out), .en(decoder_2_out1), .Q(IR_q), .clk(Clock_out));  // open: clr
  assign xor_1_out = AC_q ^ DR_q;  // XOR_Gate xor_1, 16 bits wide
  assign not_1_out = ~AC_q;  // NOT_Gate not_1, 16 bits wide
  or or_2 (or_2_out, and_5_out, and_6_out, and_4_out, and_3_out);
  Bit_Extender #(.in_width(16), .out_width(12)) bit_extender_1 (.in(multiplexer_2_out), .out(bit_extender_1_out));
  Multiplexer #(.select(3), .width(16)) multiplexer_1 (
    .in0(adder_1_out), .in1(subtractor_1_out), .in2(DR_q), .in3(and_1_out), .in4(or_1_out), .in5(xor_1_out),
    .in6(not_1_out), .out(multiplexer_1_out), .sel(priority_encoder_1_out), .en(or_2_out));  // open: in7
  Counter #(.width(12), .max('hfff)) PC (
    .load(and_11_out), .D(bit_extender_1_out), .count(or_8_out), .Q(PC_q), .clk(Clock_out));  // open: carry, clr
  Priority_Encoder priority_encoder_1 (
    .in0(and_6_out), .in1(and_5_out), .in2(and_4_out), .in3(and_3_out), .out(priority_encoder_1_out),
    .en_in(1'b1));  // open: in4, in5, in6, in7
  and and_3 (and_3_out, decoder_2_out5, decoder_1_out0);
  assign bit_extender_2_out = {{4{1'b0}}, PC_q};  // Bit_Extender bit_extender_2
  and and_4 (and_4_out, decoder_1_out2, decoder_2_out5);
  Register #(.width(16)) AC (.D(multiplexer_1_out), .en(and_13_out), .Q(AC_q), .clk(Clock_out));  // open: clr
  and and_5 (and_5_out, decoder_1_out5, decoder_2_out5);
  and and_6 (and_6_out, decoder_1_out1, decoder_2_out5);
  Register #(.width(16)) DR (.D(multiplexer_2_out), .en(and_14_out), .Q(DR_q), .clk(Clock_out));  // open: clr
  Register #(.width(16)) TR (.D(multiplexer_2_out), .en(in_1), .Q(TR_q), .clk(Clock_out));  // open: clr
  Bit_Extender #(.in_width(16), .out_width(12)) bit_extender_3 (.in(multiplexer_2_out), .out(bit_extender_3_out));
  BitSelector #(.width(16)) bitselector_1 (.in(IR_q), .out(bitselector_1_out), .sel(4'b1111));
  Counter #(.width(4), .max('hf)) Sequence_Counter (
    .Q(Sequence_Counter_q), .clk(Clock_out), .clr(d_ff_2_q));  // open: load, D, count, carry
  or or_3 (or_3_out, and_8_out, and_7_out);
  D_Flip_Flop d_ff_2 (.clk(Clock_out), .D(or_3_out), .Q(d_ff_2_q));  // open: Qn, preset, en, reset
  Register #(.width(12)) AR (.D(bit_extender_3_out), .en(or_10_out), .Q(AR_q), .clk(Clock_out));  // open: clr
  BitSelector #(.width(16), .group(4)) bitselector_2 (.in(IR_q), .out(bitselector_2_out), .sel(2'b11));
  BitSelector #(.width(4), .group(3)) bitselector_3 (.in(bitselector_2_out), .out(bitselector_3_out), .sel(1'b0));
  D_Flip_Flop I_FlipFlop (
    .clk(Clock_out), .D(bitselector_1_out), .Q(I_FlipFlop_q), .en(decoder_2_out2));  // open: Qn, preset, reset
  Decoder #(.select(3)) decoder_1 (
    .out0(decoder_1_out0), .out1(decoder_1_out1), .out2(decoder_1_out2), .out3(decoder_1_out3),
    .out4(decoder_1_out4), .out5(decoder_1_out5), .out6(decoder_1_out6), .out7(decoder_1_out7),
    .sel(bitselector_3_out));  // open: en
  not not_2 (not_2_out, I_FlipFlop_q);
  Decoder #(.select(4)) decoder_2 (
    .out0(decoder_2_out0), .out1(decoder_2_out1), .out2(decoder_2_out2), .out3(decoder_2_out3),
    .out4(decoder_2_out4), .out5(decoder_2_out5), .out6(decoder_2_out6), .out7(decoder_2_out7),
    .out8(decoder_2_out8), .out9(decoder_2_out9), .out10(decoder_2_out10), .out11(decoder_2_out11),
    .out12(decoder_2_out12), .out13(decoder_2_out13), .out14(decoder_2_out14), .out15(decoder_2_out15),
    .sel(Sequence_Counter_q));  // open: en
  Multiplexer #(.select(3), .width(16)) multiplexer_2 (
    .in0(AC_q), .in1(DR_q), .in2(TR_q), .in3(bit_extender_4_out), .in4(ram_1_data), .in5(bit_extender_2_out),
    .in6(IR_q), .out(multiplexer_2_out), .sel(priority_encoder_2_out), .en(or_14_out));  // open: in7
  assign bit_extender_4_out = {{4{1'b0}}, AR_q};  // Bit_Extender bit_extender_4
  BitSelector #(.width(16), .group(12)) bitselector_4 (.in(IR_q), .out(bitselector_4_out), .sel(1'b0));
  and and_7 (and_7_out, decoder_2_out4, or_4_out);
  Clock Clock (.out(Clock_out));
  and and_8 (and_8_out, decoder_2_out5, or_5_out);
  Demultiplexer demultiplexer_1 ();  // open: out0, out1, in, sel, en
  or or_4 (or_4_out, decoder_1_out3, decoder_1_out4);
  or or_5 (or_5_out, decoder_1_out0, decoder_1_out1, decoder_1_out2, decoder_1_out5);
  or or_6 (or_6_out, decoder_2_out1, and_10_out);
  and and_9 (and_9_out, decoder_1_out3, decoder_2_out4);
  and and_10 (and_10_out, decoder_2_out4, or_7_out);
  and and_11 (and_11_out, decoder_1_out4, decoder_2_out4);
  or or_7 (or_7_out, decoder_1_out5, decoder_1_out2, decoder_1_out1, decoder_1_out0);
  or or_8 (or_8_out, decoder_2_out1, and_12_out);
  and and_12 (and_12_out, decoder_1_out7, not_2_out, decoder_2_out3, bitselector_5_out, comparator_1_eq);
  BitSelector #(.width(12)) bitselector_5 (.in(bitselector_4_out), .out(bitselector_5_out), .sel(4'b0010));
  and and_13 (and_13_out, decoder_2_out5, or_9_out);
  Comparator #(.width(16), .mode("unsigned")) comparator_1 (
    .a(AC_q), .b({16{1'b0}}), .eq(comparator_1_eq));  // open: gt, lt
  and and_14 (and_14_out, decoder_2_out4, or_11_out);
  or or_9 (or_9_out, decoder_1_out5, decoder_1_out2, decoder_1_out1, decoder_1_out0);
  or or_10 (or_10_out, decoder_2_out0, decoder_2_out2);
  or or_11 (or_11_out, decoder_1_out5, decoder_1_out2, decoder_1_out1, decoder_1_out0);
  and and_15 (and_15_out, decoder_1_out4, decoder_2_out4);
  or or_12 (or_12_out, decoder_2_out1, and_16_out);
  and and_16 (and_16_out, decoder_2_out4, or_13_out);
  or or_13 (or_13_out, decoder_1_out5, decoder_1_out2, decoder_1_out1, decoder_1_out0);
  Priority_Encoder priority_encoder_2 (
    .in0(and_17_out), .in3(and_15_out), .in4(or_12_out), .in5(decoder_2_out0), .in6(decoder_2_out2),
    .out(priority_encoder_2_out));  // open: in1, in2, in7, en_in
  or or_14 (or_14_out, decoder_2_out2, decoder_2_out0, or_12_out, and_15_out, and_17_out);
  and and_17 (and_17_out, decoder_1_out3, decoder_2_out4);
  Controlled_Buffer controlled_buffer_1 ();  // open: in, out, en

  // Notes on the sheet:
  //   T Signals
  //   D Signals
  //   AC
  //   IR(0-11)
endmodule
